# Fritzing sketch mqtt_project (saved by Fritzing 0.9.3b)
breadboards: 2

parts:
  MH-ET_LIVE_ESP32_DEVKIT1 = MH-ET LIVE ESP32 DEVKIT 38 pins
  Mod1 = Raspberry Pi Pico W
  R1 = Resistor [tolerance=±5% resistance=220 package=THT]
  LED1 = LED - 5mm [color="Red (633nm)" package="5 mm [THT]"]
  U1 = POT [package=pot_mammoth]
  R2 = Resistor [tolerance=±5% resistance=220 package=THT]
  LED2 = LED - 5mm [color="Red (633nm)" package="5 mm [THT]"]
  U2 = POT [package=pot_mammoth]

nets:
  N1: MH-ET_LIVE_ESP32_DEVKIT1.3V3, U2.S
  N2: MH-ET_LIVE_ESP32_DEVKIT1.IO35, U2.A
  N3: MH-ET_LIVE_ESP32_DEVKIT1.IO12, LED2.anode
  N4: MH-ET_LIVE_ESP32_DEVKIT1.GND#58, R2.Pin_0, U2.E
  N5: Mod1.pin_3, Mod1.pin_8, Mod1.pin_13, Mod1.pin_18, Mod1.pin_23, Mod1.pin_28, Mod1.pin_33, Mod1.pin_38, R1.Pin_0, U1.E
  N6: Mod1.pin_7, LED1.anode
  N7: Mod1.pin_31, U1.A
  N8: Mod1.pin_36, U1.S
  N9: R1.Pin_1, LED1.cathode
  N10: R2.Pin_1, LED2.cathode

custom parts:
  MH-ET LIVE ESP32 DEVKIT 38 pins: http://mh.nodebb.com/topic/2/mh-et-live-esp32-devkit
  Raspberry Pi Pico W: Raspberry Pi Pico W. Based around the RP2040 microcontroller the Pico W is a low cost microcontroller device bringing Raspberry Pi quality, cost, and easy of use to the microcontroller space. The areas marked KEEPOUT in pcb silkscreen should not have traces running through them to avoid shorts on a soldered in module!
