# Fritzing sketch conn_sch (saved by Fritzing 0.9.3b)
breadboards: 2

parts:
  U1 = ESP32-38PinWide [part_number=ESP32-38PinWide]
  U2 = ESP32-38PinWide [part_number=ESP32-38PinWide]
  LED1 = LED - 3mm [color="Red (633nm)" package="3 mm [THT]"]
  LED2 = LED - 3mm [color="Red (633nm)" package="3 mm [THT]"]
  U3 = POT [package=pot_mammoth]
  DHT1 = Humidity and Temperature Sensor DHT11
  R1 = Resistor [tolerance=±5% resistance=220 package=THT]
  R2 = Resistor [tolerance=±5% resistance=220 package=THT]
  R3 = Resistor [tolerance=±5% resistance=220 package=THT]
  LED3 = LED - 3mm [color="Red (633nm)" package="3 mm [THT]"]
  LED4 = LED - 3mm [color="Red (633nm)" package="3 mm [THT]"]
  R4 = Resistor [tolerance=±5% resistance=220 package=THT]
  R5 = Resistor [tolerance=±5% resistance=220 package=THT]
  LED5 = LED - 3mm [color="Red (633nm)" package="3 mm [THT]"]
  R6 = Resistor [tolerance=±5% resistance=220 package=THT]
  LED6 = LED - 3mm [color="Red (633nm)" package="3 mm [THT]"]
  R7 = Resistor [tolerance=±5% resistance=220 package=THT]

nets:
  N1: U1.3.3, U3.E, DHT1.Vcc, R3.Pin_1
  N2: U1.GPIO26, DHT1.Data-signal, R3.Pin_0
  N3: U1.GPIO27, R6.Pin_1
  N4: U1.GPIO14, R2.Pin_1
  N5: U1.GPIO12, R1.Pin_1
  N6: U1.GND, LED1.cathode, LED2.cathode, U3.S, DHT1.GND_2, LED5.cathode
  N7: U2.GPIO27, R7.Pin_1
  N8: U2.GPIO14, R5.Pin_1
  N9: U2.GPIO12, R4.Pin_1
  N10: U2.GND, LED3.cathode, LED4.cathode, LED6.cathode
  N11: LED1.anode, R1.Pin_0
  N12: LED2.anode, R2.Pin_0
  N13: LED3.anode, R5.Pin_0
  N14: LED4.anode, R4.Pin_0
  N15: LED5.anode, R6.Pin_0
  N16: LED6.anode, R7.Pin_0

notes:
  SENSOR NODE
  MASTER NODE

custom parts:
  ESP32-38PinWide: Generic 38-Pin ESP32 with wide format (only access to one side of pins on a breadboard) based on Stephen Lilley's HiLetgo ESP-WROOM-32 ESP32 ESP-32S Development Board.
  Humidity and Temperature Sensor DHT11: Digital relative humidity & temperature sensor DHT11
