# Fritzing sketch webserver (saved by Fritzing 0.9.3b)
breadboards: 1

parts:
  LED1 = RGB LED (com. cathode, rgb) [package="5 mm [THT]"]
  R1 = Resistor [tolerance=±5% resistance=220 package=THT]
  R2 = Resistor [tolerance=±5% resistance=220 package=THT]
  R3 = Resistor [tolerance=±5% resistance=220 package=THT]
  LED2 = smd LED [color="Blue (470nm)" package="0603 [SMD]"]
  LED3 = smd LED [color="Orange (620nm)" package="0603 [SMD]"]
  R4 = Resistor [tolerance=±5% resistance=220 package=THT]
  R5 = Resistor [tolerance=±5% resistance=220 package=THT]
  R6 = Rotary Potentiometer (Large) [maximum_resistance=100kΩ package=THT]
  Parça1 = node32s

nets:
  N1: LED1.red_anode, R1.Pin_1
  N2: LED1.common_cathode, LED2.cathode, LED3.cathode, R6.leg1, Parça1.GND
  N3: LED1.green_anode, R2.Pin_1
  N4: LED1.blue_anode, R3.Pin_1
  N5: R1.Pin_0, Parça1.IO5
  N6: R2.Pin_0, Parça1.IO18
  N7: R3.Pin_0, Parça1.IO19
  N8: LED2.anode, R4.Pin_1
  N9: LED3.anode, R5.Pin_1
  N10: R4.Pin_0, Parça1.IO4
  N11: R5.Pin_0, Parça1.IO2
  N12: R6.wiper, Parça1.IO34
  N13: R6.leg2, Parça1.3.3V
