# Fritzing sketch w5100_connection_diagram (saved by Fritzing 0.9.3b)
breadboards: 1

parts:
  U1 = POT [package=pot_alpha_rv16af-20]
  Parça1 = Arduino Nano (Rev3.0) (ICSP)
  LED1 = RGB LED - (4 legs) [package="5 mm [THT]"]
  LED2 = LED - 5mm [color="Red (633nm)" package="5 mm [THT]"]
  WIZ820io2 = WIZ820io [part_number=WIZ820io]
  R1 = Resistor [tolerance=±5% resistance=220 package="2010 [SMD]"]
  R2 = Resistor [tolerance=±5% resistance=220 package="2010 [SMD]"]
  R3 = Resistor [tolerance=±5% resistance=220 package="2010 [SMD]"]
  R4 = Resistor [tolerance=±5% resistance=220 package="2010 [SMD]"]

nets:
  GND: U1.A, Parça1.GND, WIZ820io2.GND, R4.Pin_1
  N1: U1.S, Parça1.A0
  N2: U1.E, Parça1.5V, LED1.common_anode
  N3: Parça1.D2, LED2.anode
  N4: Parça1.D3, R1.Pin_1
  N5: Parça1.D5, R2.Pin_1
  N6: Parça1.D6, R3.Pin_1
  N7: Parça1.D8, WIZ820io2.nSS
  N8: Parça1.D11/MOSI, WIZ820io2.MOSI
  N9: Parça1.D12/MISO, WIZ820io2.MISO
  3V3: Parça1.3V3, WIZ820io2.VIN
  N10: Parça1.D13/SCK, WIZ820io2.SCLK
  N11: LED1.red_cathode, R1.Pin_0
  N12: LED1.green_cathode, R2.Pin_0
  N13: LED1.blue_cathode, R3.Pin_0
  N14: LED2.cathode, R4.Pin_0
